# Fritzing sketch Alcohol_detector (saved by Fritzing 0.9.3b)

parts:
  BAT1 = 18650 battery holder [package=battery-18650-kit]
  Part4 = Power Cell LiPo Charger/Booster
  S1 = SPST Switch [package=switch-spdt]
  U4 = Mini-360 DC-DC Buck converter [package=THT]
  Part5 = Arduino Pro Mini v13
  LED1 = smd LED [color="Red (633nm)" package="0805 [SMD]"]
  LED2 = smd LED [color="Red (633nm)" package="0805 [SMD]"]
  LED3 = smd LED [color="Yellow (595nm)" package="0805 [SMD]"]
  LED4 = smd LED [color="Yellow (595nm)" package="0805 [SMD]"]
  LED5 = smd LED [color="Blue (525nm)" package="0805 [SMD]"]
  LED6 = smd LED [color="Blue (525nm)" package="0805 [SMD]"]
  LED7 = smd LED [color="Green (565nm)" package="0805 [SMD]"]
  LED8 = smd LED [color="Green (565nm)" package="0805 [SMD]"]
  R1 = Resistor [tolerance=±5% resistance=220 package="0402 [SMD]"]
  R2 = Resistor [tolerance=±5% resistance=220 package="0402 [SMD]"]  # not connected
  R3 = Resistor [tolerance=±5% resistance=220 package="0402 [SMD]"]  # not connected
  R4 = Resistor [tolerance=±5% resistance=220 package="0402 [SMD]"]  # not connected
  R5 = Resistor [tolerance=±5% resistance=220 package="0402 [SMD]"]  # not connected
  R6 = Resistor [tolerance=±5% resistance=220 package="0402 [SMD]"]  # not connected
  R7 = Resistor [tolerance=±5% resistance=220 package="0402 [SMD]"]  # not connected
  R8 = Resistor [tolerance=±5% resistance=220 package="0402 [SMD]"]  # not connected
  Part6 = MQ-3 breakout

nets:
  N1: BAT1.+, S1.P
  N2: BAT1.-, Part4.VBATT, U4.IN-
  N3: S1.S, U4.IN+
  VCC: U4.OUT+, Part5.VCC, Part6.VCC
  N4: U4.OUT-, Part5.GND, R1.Pin_1, Part6.AO
  N5: Part5.A0, Part6.DO
  N6: Part5.D9_PWM, LED1.anode
  N7: Part5.D8, LED2.anode
  N8: Part5.D7, LED3.anode
  N9: Part5.D6_PWM, LED4.anode
  N10: Part5.D5_PWM, LED5.anode
  N11: Part5.D4, LED6.anode
  N12: Part5.D3_PWM, LED7.anode
  N13: Part5.D2, LED8.anode

custom parts:
  18650 battery holder: 18650 Battery Holder
  Mini-360 DC-DC Buck converter: Mini-360 DC-DC Buck converter. Tiny buck step down voltage converter, input voltage 4.75 to 23V output 1 to 17V adjustable. Available from ebay and the like.
  MQ-3 breakout: Alcohol sensor is capable of detecting alcohol (ethanol) particles on itself and gives the information in digital form back to us to manipulate with it. SKU:101251 • Voltage: 5V DC • Power: max 750mW • Measurement range: 0.04-4mg/L
